// Logisim project New BSPD.circ as structural Verilog: 4 circuits, main circuit main
module main (
  input  OK,
  input  RST,
  output out_3
);

  wire clock_1_out, nand_1_out, nand_2_out, state_machine_1_state_b, timing_1__5t, timing_1__10t;

  Clock clock_1 (.out(clock_1_out));
  state_machine state_machine_1 (
    .CLK(clock_1_out), ._10T(timing_1__10t), .RST(RST), ._5T(timing_1__5t), .System_OK(OK),
    .State_B(state_machine_1_state_b), .SM_OK(out_3));
  nand nand_1 (nand_1_out, out_3, out_3);
  nand nand_2 (nand_2_out, nand_1_out, state_machine_1_state_b);
  timing timing_1 (
    .CLK(clock_1_out), .RST(RST), .SD_Counting(state_machine_1_state_b), .Reset_Counting(nand_2_out),
    ._5T(timing_1__5t), ._10T(timing_1__10t));
endmodule

module mux (
  input  S,
  input  A,
  input  B,
  output Q
);

  wire nand_1_out, nand_2_out, nand_3_out;

  nand nand_1 (nand_1_out, S, S);
  nand nand_2 (nand_2_out, S, A);
  nand nand_3 (nand_3_out, nand_1_out, B);
  nand nand_4 (Q, nand_2_out, nand_3_out);

  // Notes on the sheet:
  //   S=1, Q=A
  //   S=0, Q=B
endmodule

module state_machine (
  input  CLK,
  input  _10T,
  input  RST,
  input  _5T,
  input  System_OK,
  output SM_OK,
  output State_B
);

  wire clock_1_out, mux_1_q, mux_2_q, nand_1_out, nand_2_out, nand_3_out, nand_4_out, nand_5_out, nand_6_out,
       nand_7_out, nand_8_out, nand_9_out, nand_10_out, nand_11_out, nand_12_out;

  nand nand_1 (nand_1_out, nand_2_out, nand_2_out);
  nand nand_2 (nand_2_out, System_OK, _10T);
  nand nand_3 (nand_3_out, _5T, _5T);
  nand nand_4 (nand_4_out, SM_OK, SM_OK);
  nand nand_5 (nand_5_out, nand_1_out, State_B);
  nand nand_6 (nand_6_out, SM_OK, nand_3_out);
  nand nand_7 (nand_7_out, SM_OK, State_B);
  nand nand_8 (nand_8_out, nand_4_out, State_B);
  nand nand_9 (nand_9_out, SM_OK, System_OK);
  nand nand_10 (nand_10_out, SM_OK, _5T);
  nand nand_11 (nand_11_out, nand_5_out, nand_6_out, nand_7_out);
  nand nand_12 (nand_12_out, nand_8_out, nand_9_out, nand_10_out);
  mux mux_1 (.S(RST), .A(1'b1), .B(nand_11_out), .Q(mux_1_q));
  mux mux_2 (.S(RST), .A(1'b1), .B(nand_12_out), .Q(mux_2_q));
  Clock clock_1 (.out(clock_1_out));
  D_Flip_Flop d_ff_1 (.clk(clock_1_out), .D(mux_1_q), .Q(SM_OK));  // open: Qn, preset, en, reset
  D_Flip_Flop d_ff_2 (.clk(clock_1_out), .D(mux_2_q), .Q(State_B));  // open: Qn, preset, en, reset
endmodule

module timing (
  input  CLK,
  input  RST,
  input  SD_Counting,
  input  Reset_Counting,
  output _5T,
  output _10T
);

  wire clock_1_out, nand_1_out;
  wire [10:0] counter_2_q;
  wire [11:0] counter_1_q, counter_3_q;

  Clock clock_1 (.out(clock_1_out));
  Counter #(.width(12), .max('hfff)) counter_1 (
    .count(1'b1), .Q(counter_1_q), .clk(clock_1_out), .clr(RST));  // open: load, D, carry
  Counter #(.width(12), .max('hfff)) counter_2 (
    .count(1'b1), .Q({_5T, counter_2_q}), .clk(counter_1_q[2]), .clr(SD_Counting));  // open: load, D, carry
  Counter #(.width(12), .max('hfff)) counter_3 (
    .count(1'b1), .Q(counter_3_q), .clk(counter_1_q[6]), .clr(Reset_Counting));  // open: load, D, carry
  nand nand_1 (nand_1_out, counter_3_q[9], counter_3_q[11]);
  nand nand_2 (_10T, nand_1_out, nand_1_out);
endmodule
